# Fritzing sketch Setup (saved by Fritzing 1.0.1rc)
breadboards: 1

parts:
  C1 = Electrolytic Capacitor [capacitance=480µF voltage=35V package="0605 [SMD, electrolytic]"]
  A1 = ESP32-S3 zero
  Mod1 = TMC2209 [package=THT]
  R1 = Resistor [tolerance=±5% power=0.25W resistance=1k package=THT]
  V1 = DC Power [voltage=24V]
  U1 = LMZ14203 [package=to-pmod-7]
  M1 = Stepper Motor - Bipolar

nets:
  N1: C1.-, V1.V-, U1.GND
  N2: C1.+, V1.V+, U1.VIN
  N3: A1.Pin_1, U1.VOUT
  N4: A1.Pin_3, Mod1.VIO
  N5: A1.Pin_13, Mod1.DIAG
  N6: A1.Pin_14, Mod1.EN
  N7: A1.Pin_15, Mod1.Step
  N8: A1.Pin_16, Mod1.Dir
  N9: A1.Pin_28, Mod1.UART, R1.Pin_0
  N10: A1.Pin_29, R1.Pin_1
  N11: Mod1.M1B, M1.C
  N12: Mod1.M1A, M1.A
  N13: Mod1.M2A, M1.B
  N14: Mod1.M2B, M1.D

custom parts:
  ESP32-S3 zero: ESP32-S3 Mini Development Board, Based on ESP32-S3FH4R2 Dual-Core Processor, 240MHz Running Frequency, 2.4GHz Wi-Fi & Bluetooth 5.
  TMC2209: TMC2209-LA stepper motor controller and driver. Supply voltage 4.75-28V Iphase up to 1.77A rms (2.5A peak)
